# Fritzing sketch kubo board ongoing support (saved by Fritzing 0.9.3b)
circuit board: 6cm x 6cm
breadboards: 1

parts:
  Tact1 = Pushbutton [package="[THT]"]
  CD4021B = IC, DIP package, 16 pins [chip_label=CD4021B]
  Limit_1 = female pin header, 5 pins [form="♀ (female)"]
  Input = female pin header, 5 pins [form="♀ (female)"]
  Output = female pin header, 5 pins [form="♀ (female)"]
  Tact2 = Pushbutton [package="[THT]"]
  Limit_2 = female pin header, 5 pins [form="♀ (female)"]
  Tact3 = Pushbutton [package="[THT]"]
  Limit_3 = female pin header, 5 pins [form="♀ (female)"]
  Tact4 = Pushbutton [package="[THT]"]
  Limit_4 = female pin header, 5 pins [form="♀ (female)"]
  LED1 = smd LED [color="Red (633nm)" package="0805 [SMD]"]
  R1 = Resistor [tolerance=±5% resistance=300 package="0805 [SMD]"]
  LED2 = smd LED [color="Red (633nm)" package="0805 [SMD]"]
  R2 = Resistor [tolerance=±5% resistance=300 package="0805 [SMD]"]
  LED3 = smd LED [color="Red (633nm)" package="0805 [SMD]"]
  R3 = Resistor [tolerance=±5% resistance=300 package="0805 [SMD]"]
  LED4 = smd LED [color="Red (633nm)" package="0805 [SMD]"]
  R4 = Resistor [tolerance=±5% resistance=300 package="0805 [SMD]"]
  LED5 = smd LED [color="Red (633nm)" package="0805 [SMD]"]
  R5 = Resistor [tolerance=±5% resistance=300 package="0805 [SMD]"]
  LED6 = smd LED [color="Red (633nm)" package="0805 [SMD]"]
  R6 = Resistor [tolerance=±5% resistance=300 package="0805 [SMD]"]
  LED7 = smd LED [color="Red (633nm)" package="0805 [SMD]"]
  R7 = Resistor [tolerance=±5% resistance=300 package="0805 [SMD]"]
  LED8 = smd LED [color="Red (633nm)" package="0805 [SMD]"]
  R8 = Resistor [tolerance=±5% resistance=300 package="0805 [SMD]"]
  R9 = Resistor [tolerance=±5% resistance=10k package=THT]
  R10 = Resistor [tolerance=±5% resistance=10k package=THT]
  R11 = Resistor [tolerance=±5% resistance=10k package=THT]
  R12 = Resistor [tolerance=±5% resistance=10k package=THT]

nets:
  C1: Tact1.Pin_1, Tact1.Pin_2, CD4021B.pin15, Limit_1.pin3, R9.Pin_1
  5V: Tact1.Pin_3, Tact1.Pin_4, CD4021B.pin16, Limit_1.pin1, Input.pin5, Output.pin5, Tact2.Pin_3, Tact2.Pin_4, Limit_2.pin1, Tact3.Pin_3, Tact3.Pin_4, Limit_3.pin1, Tact4.Pin_3, Tact4.Pin_4, Limit_4.pin1, R1.Pin_0, R2.Pin_0, R3.Pin_0, R4.Pin_0, R5.Pin_0, R6.Pin_0, R7.Pin_0, R8.Pin_0
  GND: CD4021B.pin1, CD4021B.pin5, CD4021B.pin6, CD4021B.pin8, CD4021B.pin14, Input.pin1, Output.pin1, LED1.cathode, LED2.cathode, LED3.cathode, LED4.cathode, LED5.cathode, LED6.cathode, LED7.cathode, LED8.cathode, R9.Pin_0, R10.Pin_0, R11.Pin_0, R12.Pin_0
  OUT: CD4021B.pin3, Output.pin2
  C3: CD4021B.pin4, Tact3.Pin_1, Tact3.Pin_2, Limit_3.pin3, R11.Pin_1
  C4: CD4021B.pin7, Tact4.Pin_1, Tact4.Pin_2, Limit_4.pin3, R12.Pin_1
  Latch: CD4021B.pin9, Input.pin3, Output.pin3
  Clock: CD4021B.pin10, Input.pin4, Output.pin4
  IN: CD4021B.pin11, Input.pin2
  C2: CD4021B.pin13, Tact2.Pin_1, Tact2.Pin_2, Limit_2.pin3, R10.Pin_1
  N1: LED1.anode, R1.Pin_1
  N2: LED2.anode, R2.Pin_1
  N3: LED3.anode, R3.Pin_1
  N4: LED4.anode, R4.Pin_1
  N5: LED5.anode, R5.Pin_1
  N6: LED6.anode, R6.Pin_1
  N7: LED7.anode, R7.Pin_1
  N8: LED8.anode, R8.Pin_1

notes:
  GND
  V++
  s1-p7
  s2-p5
  s3-p4
  s4-p1
  p2,3,6,8 nc
  KUBO!
