# Fritzing sketch protoboard layout (saved by Fritzing 0.9.3b)
perfboards: 1

parts:
  IC1 = IC, DIP package, 16 pins [chip_label=CD4021B]  # not connected
  S1 = Pushbutton [package="[THT]"]
  S2 = Pushbutton [package="[THT]"]
  S3 = Pushbutton [package="[THT]"]
  S4 = Pushbutton [package="[THT]"]
  J1 = male pin header, 5 pins [form="♂ (male)"]  # not connected
  J2 = male pin header, 5 pins [form="♂ (male)"]  # not connected
  R1 = Resistor [tolerance=±10% resistance=10k package=THT]  # not connected
  R2 = Resistor [tolerance=±10% resistance=10k package=THT]  # not connected

nets:
  N1: S1.Pin_1, S1.Pin_2
  N2: S1.Pin_3, S1.Pin_4
  N3: S2.Pin_1, S2.Pin_2
  N4: S2.Pin_3, S2.Pin_4
  N5: S3.Pin_1, S3.Pin_2
  N6: S3.Pin_3, S3.Pin_4
  N7: S4.Pin_1, S4.Pin_2
  N8: S4.Pin_3, S4.Pin_4
